// Logisim project Bird.circ as structural Verilog: 10 circuits, main circuit main
module main (
  input  stackCLR,
  input  [15:0] in_2
);

  wire AFA_out, BFA_out, CLOCK_out, cpu_1_memld, not_1_out, not_2_out, not_3_out, not_4_out, not_5_out,
       not_6_out, not_7_out, or_1_out, pop_1_dout, READY_out;
  wire [1:0] priority_encoder_1_out;
  wire [3:0] n16_bit_register_1_q;
  wire [11:0] cpu_1_addr;
  wire [15:0] controlled_buffer_1_out, cpu_1_dout, io_device_1_d_out, Memory_Output, multiplexer_1_out,
       multiplexer_2_out, multiplexer_3_out;
  wire [15:4] n16_bit_register_1_q_2;

  Button READY (.out(READY_out));
  IO_device io_device_1 (
    .d_in(in_2), .d_out(io_device_1_d_out), .ready(READY_out), .device_addr(AFA_out), .a0(cpu_1_addr[0]));
  Multiplexer #(.select(2), .width(16), .enable("false")) multiplexer_1 (
    .in0({16{1'b0}}), .in1(Memory_Output), .in2(io_device_1_d_out), .out(multiplexer_1_out),
    .sel(priority_encoder_1_out));  // open: in3
  Priority_Encoder #(.select(2)) priority_encoder_1 (
    .in0(1'b1), .in1(not_1_out), .in2(AFA_out), .out(priority_encoder_1_out));  // open: in3
  not not_1 (not_1_out, AFA_out);
  and AFA (AFA_out, cpu_1_addr[11], not_3_out, cpu_1_addr[9], not_2_out, cpu_1_addr[7], cpu_1_addr[6], cpu_1_addr[5], cpu_1_addr[4], cpu_1_addr[3], not_4_out, cpu_1_addr[1]);
  not not_2 (not_2_out, cpu_1_addr[8]);
  not not_3 (not_3_out, cpu_1_addr[10]);
  POP pop_1 (.Din(multiplexer_1_out), .clk(CLOCK_out), .Dout(pop_1_dout));
  not not_4 (not_4_out, cpu_1_addr[2]);
  CPU cpu_1 (
    .Din(multiplexer_1_out), .Clrstack(stackCLR), .Dout(cpu_1_dout), .Addr(cpu_1_addr), .CLOCK(CLOCK_out),
    .MEMLD(cpu_1_memld));
  Multiplexer #(.width(16), .enable("false")) multiplexer_2 (
    .in0(multiplexer_3_out), .in1({16{1'b0}}), .out(multiplexer_2_out), .sel(pop_1_dout));
  Multiplexer #(.width(16), .enable("false")) multiplexer_3 (
    .in0(cpu_1_dout), .in1(io_device_1_d_out), .out(multiplexer_3_out), .sel(AFA_out));
  or or_1 (or_1_out, cpu_1_memld, pop_1_dout, AFA_out);
  RAM #(.addrWidth(12), .dataWidth(16), .bus("separate")) ram_1 (
    .addr(cpu_1_addr), .din(multiplexer_2_out), .data(Memory_Output), .str(or_1_out), .clk(CLOCK_out));  // open: sel, ld, clr
  not not_5 (not_5_out, cpu_1_addr[0]);
  not not_6 (not_6_out, cpu_1_addr[2]);
  assign controlled_buffer_1_out = BFA_out ? Memory_Output : 16'bz;  // Controlled_Buffer controlled_buffer_1
  and BFA (BFA_out, not_5_out, cpu_1_addr[1], not_6_out, cpu_1_addr[3], cpu_1_addr[4], cpu_1_addr[5], cpu_1_addr[6], cpu_1_addr[7], cpu_1_addr[8], cpu_1_addr[9], not_7_out, cpu_1_addr[11]);
  not not_7 (not_7_out, cpu_1_addr[10]);
  _16_bit_register u_16_bit_register_1 (
    .D(controlled_buffer_1_out), .load(BFA_out), .clock(CLOCK_out),
    .Q({n16_bit_register_1_q_2, n16_bit_register_1_q}));
  Hex_Digit_Display hex_digit_display_1 (.value(n16_bit_register_1_q_2[15:12]));  // open: dp
  Hex_Digit_Display hex_digit_display_2 (.value(n16_bit_register_1_q_2[11:8]));  // open: dp
  Clock CLOCK (.out(CLOCK_out));
  Hex_Digit_Display hex_digit_display_3 (.value(n16_bit_register_1_q_2[7:4]));  // open: dp
  Hex_Digit_Display hex_digit_display_4 (.value(n16_bit_register_1_q));  // open: dp
endmodule

// IO Device
module IO_device (
  input  [15:0] d_in,
  input  ready,
  input  device_addr,
  input  a0,
  output [15:0] d_out
);

  wire and_1_out, not_1_out;
  wire [2:2] register_2_q;
  wire [15:0] register_1_q;

  Register #(.width(16)) register_1 (.D(d_in), .en(1'b1), .Q(register_1_q), .clk(register_2_q[2]));  // open: clr
  Register #(.width(1)) register_2 (.D(1'b1), .en(1'b1), .Q(register_2_q[2]), .clk(ready), .clr(and_1_out));
  and and_1 (and_1_out, device_addr, not_1_out);
  not not_1 (not_1_out, a0);
  Multiplexer #(.width(16), .enable("false")) multiplexer_1 (
    .in0(register_1_q), .in1({{13{1'b0}}, register_2_q[2], 2'b00}), .out(d_out), .sel(a0));

  // Notes on the sheet:
  //   Whenever a0=0, CPU gets the DATA register
endmodule

module CPU (
  input  CLOCK,
  input  [15:0] Din,
  input  Clrstack,
  output [15:0] Dout,
  output [11:0] Addr,
  output MEMLD
);

  wire alu_1_zf, DATAMUX, IRLD, MUX, PC_INC, PC_LD, PC_MUX, REGLD, SPDEC, SPINC, ZF, ZFLD;
  wire [1:0] ADDRMUX;
  wire [3:0] multiplexer_4_out_2, multiplexer_6_out_2, register_bank_1_reg7_stack_register_2;
  wire [11:0] adder_1_out, multiplexer_2_out, multiplexer_4_out, multiplexer_6_out, pc_1_out,
       register_bank_1_reg7_stack_register;
  wire [15:0] alu_1_out, IR_Cable, register_bank_1_reg0, register_bank_1_reg1, register_bank_1_reg2,
       register_bank_1_reg3, register_bank_1_reg4, register_bank_1_reg5, register_bank_1_reg6, src2;

  Multiplexer #(.select(2), .width(12), .enable("false")) multiplexer_1 (
    .in0(pc_1_out), .in1(multiplexer_6_out), .in2(register_bank_1_reg7_stack_register), .out(Addr),
    .sel(ADDRMUX));  // open: in3
  pc pc_1 (.out(pc_1_out), .clk(CLOCK), .PC_INC(PC_INC), .\input (multiplexer_2_out), .PC_LD(PC_LD));
  Multiplexer #(.width(12), .enable("false")) multiplexer_2 (
    .in0(adder_1_out), .in1(multiplexer_4_out), .out(multiplexer_2_out), .sel(PC_MUX));
  Adder #(.width(12)) adder_1 (.a(pc_1_out), .b(IR_Cable[11:0]), .out(adder_1_out));  // open: cin, cout
  Multiplexer #(.width(16), .enable("false")) multiplexer_3 (
    .in0({4'b0000, pc_1_out}), .in1(src2), .out(Dout), .sel(DATAMUX));
  _16_bit_register u_16_bit_register_1 (.D(Din), .load(IRLD), .clock(CLOCK), .Q(IR_Cable));
  Multiplexer #(.width(16), .enable("false")) multiplexer_4 (
    .in0(Din), .in1(alu_1_out), .out({multiplexer_4_out_2, multiplexer_4_out}), .sel(MUX));
  register_bank register_bank_1 (
    .D_in({multiplexer_4_out_2, multiplexer_4_out}), .REGSEL(IR_Cable[2:0]), .reg0(register_bank_1_reg0),
    .reg2(register_bank_1_reg2), .REGLD(REGLD), .reg1(register_bank_1_reg1), .reg3(register_bank_1_reg3),
    .clk(CLOCK), .reg4(register_bank_1_reg4), .reg5(register_bank_1_reg5), .reg6(register_bank_1_reg6),
    .reg7_Stack_Register({register_bank_1_reg7_stack_register_2, register_bank_1_reg7_stack_register}),
    .SPINC(SPINC), .SPDEC(SPDEC), .clr_stack(Clrstack));
  Multiplexer #(.select(3), .width(16), .enable("false")) multiplexer_5 (
    .in0(register_bank_1_reg0), .in1(register_bank_1_reg1), .in2(register_bank_1_reg2),
    .in3(register_bank_1_reg3), .in4(register_bank_1_reg4), .in5(register_bank_1_reg5),
    .in6(register_bank_1_reg6),
    .in7({register_bank_1_reg7_stack_register_2, register_bank_1_reg7_stack_register}), .out(src2),
    .sel(IR_Cable[8:6]));
  ALU alu_1 (
    .in1({multiplexer_6_out_2, multiplexer_6_out}), .in2(src2), .ALU_EXTRA(IR_Cable[8:6]),
    .ALUSEL(IR_Cable[11:9]), .out(alu_1_out), .ZF(alu_1_zf));
  Register #(.width(1)) register_1 (.D(alu_1_zf), .en(ZFLD), .Q(ZF), .clk(CLOCK));  // open: clr
  Multiplexer #(.select(3), .width(16), .enable("false")) multiplexer_6 (
    .in0(register_bank_1_reg0), .in1(register_bank_1_reg1), .in2(register_bank_1_reg2),
    .in3(register_bank_1_reg3), .in4(register_bank_1_reg4), .in5(register_bank_1_reg5),
    .in6(register_bank_1_reg6),
    .in7({register_bank_1_reg7_stack_register_2, register_bank_1_reg7_stack_register}),
    .out({multiplexer_6_out_2, multiplexer_6_out}), .sel(IR_Cable[5:3]));
  control_unit control_unit_1 (
    .clock(CLOCK), .opcode(Din), .zf(ZF), .MUX(MUX), .PCLD(PC_LD), .PCINC(PC_INC), .IRLD(IRLD),
    .REGLD(REGLD), .MEMLD(MEMLD), .ZFLD(ZFLD), .SPINC(SPINC), .SPDEC(SPDEC), .PCMUX(PC_MUX),
    .DATAMUX(DATAMUX), .ADDRMUX(ADDRMUX));

  // Other names for the same wires on the sheet: Imm[15:0] = Din

  // Notes on the sheet:
  //   DataMux=1 ; MEM[sp]=PC (call operation)
  //   mem[src2] = src1 (LOAD & STORE)
  //   pc = ir + pc (jump operation)
  //   pc is set to stack register's content!
  //   Source #2
  //   Source #1
endmodule

// Register Bank
module register_bank (
  input  clk,
  input  [2:0] REGSEL,
  input  SPINC,
  input  SPDEC,
  input  clr_stack,
  input  REGLD,
  input  [15:0] D_in,
  output [15:0] reg0,
  output [15:0] reg1,
  output [15:0] reg2,
  output [15:0] reg3,
  output [15:0] reg4,
  output [15:0] reg5,
  output [15:0] reg6,
  output [15:0] reg7_Stack_Register
);

  wire and_1_out, and_2_out, and_3_out, and_4_out, and_5_out, and_6_out, and_7_out, and_8_out,
       demultiplexer_1_out0, demultiplexer_1_out1, demultiplexer_1_out2, demultiplexer_1_out3,
       demultiplexer_1_out4, demultiplexer_1_out5, demultiplexer_1_out6, demultiplexer_1_out7, or_1_out,
       or_2_out;

  Demultiplexer #(.select(3), .enable("false")) demultiplexer_1 (
    .out0(demultiplexer_1_out0), .out1(demultiplexer_1_out1), .out2(demultiplexer_1_out2),
    .out3(demultiplexer_1_out3), .out4(demultiplexer_1_out4), .out5(demultiplexer_1_out5),
    .out6(demultiplexer_1_out6), .out7(demultiplexer_1_out7), .in(1'b1), .sel(REGSEL));
  and and_1 (and_1_out, demultiplexer_1_out0, REGLD);
  and and_2 (and_2_out, demultiplexer_1_out1, REGLD);
  and and_3 (and_3_out, demultiplexer_1_out2, REGLD);
  and and_4 (and_4_out, demultiplexer_1_out3, REGLD);
  and and_5 (and_5_out, demultiplexer_1_out4, REGLD);
  and and_6 (and_6_out, demultiplexer_1_out5, REGLD);
  and and_7 (and_7_out, demultiplexer_1_out6, REGLD);
  and and_8 (and_8_out, demultiplexer_1_out7, REGLD);
  _16_bit_register u_16_bit_register_1 (.D(D_in), .load(and_1_out), .clock(clk), .Q(reg0));
  _16_bit_register u_16_bit_register_2 (.D(D_in), .load(and_2_out), .clock(clk), .Q(reg1));
  _16_bit_register u_16_bit_register_3 (.D(D_in), .load(and_3_out), .clock(clk), .Q(reg2));
  _16_bit_register u_16_bit_register_4 (.D(D_in), .load(and_4_out), .clock(clk), .Q(reg3));
  _16_bit_register u_16_bit_register_5 (.D(D_in), .load(and_5_out), .clock(clk), .Q(reg4));
  _16_bit_register u_16_bit_register_6 (.D(D_in), .load(and_6_out), .clock(clk), .Q(reg5));
  _16_bit_register u_16_bit_register_7 (.D(D_in), .load(and_7_out), .clock(clk), .Q(reg6));
  or or_1 (or_1_out, SPDEC, and_8_out);
  or or_2 (or_2_out, SPINC, SPDEC);
  Counter #(.width(16), .max('hffff)) counter_1 (
    .load(or_1_out), .D(D_in), .count(or_2_out), .Q(reg7_Stack_Register), .clk(clk), .clr(clr_stack));  // open: carry
endmodule

module ALU (
  input  [15:0] in1,
  input  [15:0] in2,
  input  [2:0] ALU_EXTRA,
  input  [2:0] ALUSEL,
  output [15:0] out,
  output ZF
);

  wire or_2_out;
  wire [15:0] adder_1_out, adder_2_out, and_1_out, multiplexer_2_out, not_1_out, or_1_out, subtractor_1_out,
       subtractor_2_out, xor_1_out;

  Adder #(.width(16)) adder_1 (.a(in1), .b(in2), .out(adder_1_out));  // open: cin, cout
  Subtractor #(.width(16)) subtractor_1 (.a(in1), .b(in2), .out(subtractor_1_out));  // open: bin, bout
  assign or_1_out = in1 | in2;  // OR_Gate or_1, 16 bits wide
  assign and_1_out = in1 & in2;  // AND_Gate and_1, 16 bits wide
  Multiplexer #(.select(3), .width(16), .enable("false")) multiplexer_1 (
    .in0(adder_1_out), .in1(subtractor_1_out), .in2(and_1_out), .in3(or_1_out), .in4(xor_1_out),
    .in7(multiplexer_2_out), .out(out), .sel(ALUSEL));  // open: in5, in6
  assign xor_1_out = in1 ^ in2;  // XOR_Gate xor_1, 16 bits wide
  assign not_1_out = ~in1;  // NOT_Gate not_1, 16 bits wide
  Multiplexer #(.select(3), .width(16), .enable("false")) multiplexer_2 (
    .in0(in1), .in1(not_1_out), .in2(adder_2_out), .in3(subtractor_2_out), .out(multiplexer_2_out),
    .sel(ALU_EXTRA));  // open: in4, in5, in6, in7
  Adder #(.width(16)) adder_2 (.a(in1), .b(16'h1), .out(adder_2_out));  // open: cin, cout
  or or_2 (or_2_out, out[0], out[1], out[2], out[3], out[4], out[5], out[6], out[7], out[8], out[9], out[10], out[11], out[12], out[13], out[14], out[15]);
  not not_2 (ZF, or_2_out);
  Subtractor #(.width(16)) subtractor_2 (.a(in1), .b(16'h1), .out(subtractor_2_out));  // open: bin, bout
endmodule

// PC
module pc (
  input  clk,
  input  [11:0] \input ,
  input  PC_LD,
  input  PC_INC,
  output [11:0] out
);

  wire or_1_out;
  wire [11:0] adder_1_out, multiplexer_1_out;

  Multiplexer #(.width(12), .enable("false")) multiplexer_1 (
    .in0(adder_1_out), .in1(\input ), .out(multiplexer_1_out), .sel(PC_LD));
  Adder #(.width(12)) adder_1 (.a(out), .b(12'h1), .out(adder_1_out));  // open: cin, cout
  _12_bit_register pc_Register (.clk(clk), .D(multiplexer_1_out), .load(or_1_out), .Q(out));
  or or_1 (or_1_out, PC_LD, PC_INC);
endmodule

// Control Unit
module control_unit (
  input  clock,
  input  zf,
  input  [15:0] opcode,
  output MUX,
  output PCLD,
  output PCINC,
  output IRLD,
  output REGLD,
  output MEMLD,
  output ZFLD,
  output SPINC,
  output SPDEC,
  output PCMUX,
  output DATAMUX,
  output [1:0] ADDRMUX
);

  wire fetch, not_1_out, not_2_out, not_3_out, not_4_out, not_5_out, not_6_out, not_7_out, not_8_out,
       not_9_out;
  wire [1:0] and_2_out;
  wire [1:1] and_1_out;
  wire [3:0] multiplexer_1_out, multiplexer_2_out, multiplexer_3_out, s_r_ff_1_q;
  wire [13:2] rom_1_data;

  and and_1 (and_1_out[1], not_1_out, opcode[14], not_2_out, opcode[12]);
  not not_1 (not_1_out, opcode[15]);
  not not_2 (not_2_out, opcode[13]);
  Multiplexer #(.select(2), .width(4), .enable("false")) multiplexer_1 (
    .in0(4'b0000), .in1(4'b1100), .in2(4'b1101), .out(multiplexer_1_out), .sel(and_2_out));  // open: in3
  Multiplexer #(.width(4), .enable("false")) multiplexer_2 (
    .in0(multiplexer_1_out), .in1(multiplexer_3_out), .out(multiplexer_2_out), .sel(fetch));
  Multiplexer #(.select(2), .width(4), .enable("false")) multiplexer_3 (
    .in0(opcode[15:12]), .in1(opcode[15:12]), .in2(4'b0000), .in3(4'b0100), .out(multiplexer_3_out),
    .sel({and_1_out[1], zf}));
  and and_2 (and_2_out[0], s_r_ff_1_q[0], not_7_out, not_8_out, s_r_ff_1_q[3]);
  and and_3 (and_2_out[1], s_r_ff_1_q[0], s_r_ff_1_q[1], not_9_out, s_r_ff_1_q[3]);
  not not_3 (not_3_out, multiplexer_2_out[0]);
  not not_4 (not_4_out, multiplexer_2_out[1]);
  not not_5 (not_5_out, multiplexer_2_out[2]);
  not not_6 (not_6_out, multiplexer_2_out[3]);
  not not_7 (not_7_out, s_r_ff_1_q[1]);
  not not_8 (not_8_out, s_r_ff_1_q[2]);
  not not_9 (not_9_out, s_r_ff_1_q[2]);
  S_R_Flip_Flop s_r_ff_1 (
    .S(multiplexer_2_out[0]), .clk(clock), .R(not_3_out), .Q(s_r_ff_1_q[0]), .en(1'b1));  // open: Qn, preset, reset
  S_R_Flip_Flop s_r_ff_2 (
    .S(multiplexer_2_out[1]), .clk(clock), .R(not_4_out), .Q(s_r_ff_1_q[1]), .en(1'b1));  // open: Qn, preset, reset
  S_R_Flip_Flop s_r_ff_3 (
    .S(multiplexer_2_out[2]), .clk(clock), .R(not_5_out), .Q(s_r_ff_1_q[2]), .en(1'b1));  // open: Qn, preset, reset
  S_R_Flip_Flop s_r_ff_4 (
    .S(multiplexer_2_out[3]), .clk(clock), .R(not_6_out), .Q(s_r_ff_1_q[3]), .en(1'b1));  // open: Qn, preset, reset
  ROM #(.addrWidth(4), .dataWidth(14)) rom_1 (
    .addr(s_r_ff_1_q),
    .data({rom_1_data[13], DATAMUX, PCMUX, SPDEC, SPINC, ZFLD, MEMLD, REGLD, IRLD, PCINC, PCLD, rom_1_data[2], MUX, fetch}));  // open: sel
  Multiplexer #(.select(4), .width(2), .enable("false")) multiplexer_4 (
    .in0(2'b00), .in1(2'b00), .in2(2'b01), .in3(2'b01), .in4(2'b00), .in5(2'b00), .in6(2'b00), .in7(2'b00),
    .in8(2'b10), .in9(2'b00), .in10(2'b10), .in11(2'b00), .in12(2'b10), .in13(2'b10), .in14(2'b00),
    .in15(2'b00), .out(ADDRMUX), .sel(s_r_ff_1_q));

  // Notes on the sheet:
  //   contents of rom_1 (hex, n*v repeats v):
  //   31 50 44 1084 8 8 0 142 1484 200 48c 200 44 a0c
  //   Next Line
endmodule

// IR
module _16_bit_register (
  input  [15:0] D,
  input  load,
  input  clock,
  output [15:0] Q
);

  wire not_1_out, not_2_out, not_3_out, not_4_out, not_5_out, not_6_out, not_7_out, not_8_out, not_9_out,
       not_10_out, not_11_out, not_12_out, not_13_out, not_14_out, not_15_out, not_16_out;

  not not_1 (not_1_out, D[5]);
  not not_2 (not_2_out, D[4]);
  not not_3 (not_3_out, D[3]);
  not not_4 (not_4_out, D[1]);
  not not_5 (not_5_out, D[0]);
  not not_6 (not_6_out, D[2]);
  not not_7 (not_7_out, D[6]);
  not not_8 (not_8_out, D[7]);
  not not_9 (not_9_out, D[14]);
  not not_10 (not_10_out, D[8]);
  not not_11 (not_11_out, D[13]);
  not not_12 (not_12_out, D[11]);
  not not_13 (not_13_out, D[9]);
  not not_14 (not_14_out, D[10]);
  not not_15 (not_15_out, D[12]);
  not not_16 (not_16_out, D[15]);
  S_R_Flip_Flop s_r_ff_1 (.S(D[1]), .clk(clock), .R(not_4_out), .Q(Q[1]), .en(load));  // open: Qn, preset, reset
  S_R_Flip_Flop s_r_ff_2 (.S(D[3]), .clk(clock), .R(not_3_out), .Q(Q[3]), .en(load));  // open: Qn, preset, reset
  S_R_Flip_Flop s_r_ff_3 (.S(D[5]), .clk(clock), .R(not_1_out), .Q(Q[5]), .en(load));  // open: Qn, preset, reset
  S_R_Flip_Flop s_r_ff_4 (.S(D[7]), .clk(clock), .R(not_8_out), .Q(Q[7]), .en(load));  // open: Qn, preset, reset
  S_R_Flip_Flop s_r_ff_5 (.S(D[9]), .clk(clock), .R(not_13_out), .Q(Q[9]), .en(load));  // open: Qn, preset, reset
  S_R_Flip_Flop s_r_ff_6 (.S(D[11]), .clk(clock), .R(not_12_out), .Q(Q[11]), .en(load));  // open: Qn, preset, reset
  S_R_Flip_Flop s_r_ff_7 (.S(D[13]), .clk(clock), .R(not_11_out), .Q(Q[13]), .en(load));  // open: Qn, preset, reset
  S_R_Flip_Flop s_r_ff_8 (.S(D[15]), .clk(clock), .R(not_16_out), .Q(Q[15]), .en(load));  // open: Qn, preset, reset
  S_R_Flip_Flop s_r_ff_9 (.S(D[0]), .clk(clock), .R(not_5_out), .Q(Q[0]), .en(load));  // open: Qn, preset, reset
  S_R_Flip_Flop s_r_ff_10 (.S(D[2]), .clk(clock), .R(not_6_out), .Q(Q[2]), .en(load));  // open: Qn, preset, reset
  S_R_Flip_Flop s_r_ff_11 (.S(D[4]), .clk(clock), .R(not_2_out), .Q(Q[4]), .en(load));  // open: Qn, preset, reset
  S_R_Flip_Flop s_r_ff_12 (.S(D[6]), .clk(clock), .R(not_7_out), .Q(Q[6]), .en(load));  // open: Qn, preset, reset
  S_R_Flip_Flop s_r_ff_13 (.S(D[8]), .clk(clock), .R(not_10_out), .Q(Q[8]), .en(load));  // open: Qn, preset, reset
  S_R_Flip_Flop s_r_ff_14 (.S(D[10]), .clk(clock), .R(not_14_out), .Q(Q[10]), .en(load));  // open: Qn, preset, reset
  S_R_Flip_Flop s_r_ff_15 (.S(D[12]), .clk(clock), .R(not_15_out), .Q(Q[12]), .en(load));  // open: Qn, preset, reset
  S_R_Flip_Flop s_r_ff_16 (.S(D[14]), .clk(clock), .R(not_9_out), .Q(Q[14]), .en(load));  // open: Qn, preset, reset

  // Other names for the same wires on the sheet: a[8:0] = D[8:0]; b[6:0] = D[15:9]
endmodule

module _12_bit_register (
  input  clk,
  input  [11:0] D,
  input  load,
  output [11:0] Q
);

  wire not_1_out, not_2_out, not_3_out, not_4_out, not_5_out, not_6_out, not_7_out, not_8_out, not_9_out,
       not_10_out, not_11_out, not_12_out;

  not not_1 (not_1_out, D[0]);
  not not_2 (not_2_out, D[1]);
  not not_3 (not_3_out, D[2]);
  not not_4 (not_4_out, D[3]);
  not not_5 (not_5_out, D[4]);
  not not_6 (not_6_out, D[5]);
  not not_7 (not_7_out, D[6]);
  not not_8 (not_8_out, D[7]);
  not not_9 (not_9_out, D[8]);
  not not_10 (not_10_out, D[9]);
  not not_11 (not_11_out, D[10]);
  not not_12 (not_12_out, D[11]);
  S_R_Flip_Flop s_r_ff_1 (.S(D[0]), .clk(clk), .R(not_1_out), .Q(Q[0]), .en(load));  // open: Qn, preset, reset
  S_R_Flip_Flop s_r_ff_2 (.S(D[1]), .clk(clk), .R(not_2_out), .Q(Q[1]), .en(load));  // open: Qn, preset, reset
  S_R_Flip_Flop s_r_ff_3 (.S(D[2]), .clk(clk), .R(not_3_out), .Q(Q[2]), .en(load));  // open: Qn, preset, reset
  S_R_Flip_Flop s_r_ff_4 (.S(D[3]), .clk(clk), .R(not_4_out), .Q(Q[3]), .en(load));  // open: Qn, preset, reset
  S_R_Flip_Flop s_r_ff_5 (.S(D[4]), .clk(clk), .R(not_5_out), .Q(Q[4]), .en(load));  // open: Qn, preset, reset
  S_R_Flip_Flop s_r_ff_6 (.S(D[5]), .clk(clk), .R(not_6_out), .Q(Q[5]), .en(load));  // open: Qn, preset, reset
  S_R_Flip_Flop s_r_ff_7 (.S(D[6]), .clk(clk), .R(not_7_out), .Q(Q[6]), .en(load));  // open: Qn, preset, reset
  S_R_Flip_Flop s_r_ff_8 (.S(D[7]), .clk(clk), .R(not_8_out), .Q(Q[7]), .en(load));  // open: Qn, preset, reset
  S_R_Flip_Flop s_r_ff_9 (.S(D[8]), .clk(clk), .R(not_9_out), .Q(Q[8]), .en(load));  // open: Qn, preset, reset
  S_R_Flip_Flop s_r_ff_10 (.S(D[9]), .clk(clk), .R(not_10_out), .Q(Q[9]), .en(load));  // open: Qn, preset, reset
  S_R_Flip_Flop s_r_ff_11 (.S(D[10]), .clk(clk), .R(not_11_out), .Q(Q[10]), .en(load));  // open: Qn, preset, reset
  S_R_Flip_Flop s_r_ff_12 (.S(D[11]), .clk(clk), .R(not_12_out), .Q(Q[11]), .en(load));  // open: Qn, preset, reset
endmodule

// POP CLEAR
module POP (
  input  clk,
  input  [15:0] Din,
  output Dout
);

  wire and_1_out, and_2_out, not_1_out, not_2_out, not_3_out, or_1_out, register_1_q, register_3_q;

  not not_1 (not_1_out, Din[13]);
  not not_2 (not_2_out, Din[14]);
  not not_3 (not_3_out, Din[14]);
  and and_1 (and_1_out, Din[12], not_1_out, not_2_out, Din[15]);
  and and_2 (and_2_out, Din[12], Din[13], not_3_out, Din[15]);
  or or_1 (or_1_out, and_1_out, and_2_out);
  Register #(.width(1)) register_1 (.D(or_1_out), .Q(register_1_q), .clk(clk));  // open: en, clr
  Register #(.width(1)) register_2 (.D(register_1_q), .Q(Dout), .clk(clk), .clr(register_3_q));  // open: en
  Register #(.width(1)) register_3 (.D(Dout), .Q(register_3_q), .clk(clk));  // open: en, clr

  // Notes on the sheet:
  //   If the OPCODE=POP, then after 2 clock cycles the content of the current address will be zero.
endmodule
