// Logisim project Frog.circ as structural Verilog: 7 circuits, main circuit main
module main (
);

  wire clock_1_out, IRLD, MUX, PC_INC, REGLOAD;
  wire [7:0] pc_1_out;
  wire [15:0] alu_1_out, Imm, multiplexer_1_out, multiplexer_2_out, multiplexer_3_out, n16_bit_register_1_q,
       register_bank_1_reg0, register_bank_1_reg1, register_bank_1_reg2, register_bank_1_reg3;

  pc pc_1 (.clk(clock_1_out), .PC_INC(PC_INC), .out(pc_1_out));
  ROM #(.dataWidth(16)) rom_1 (.addr(pc_1_out), .data(Imm));  // open: sel
  register_bank register_bank_1 (
    .D_in(multiplexer_1_out), .REGSEL(n16_bit_register_1_q[1:0]), .reg0(register_bank_1_reg0),
    .reg2(register_bank_1_reg2), .REGLD(REGLOAD), .reg1(register_bank_1_reg1), .reg3(register_bank_1_reg3),
    .clk(clock_1_out));
  _16_bit_register u_16_bit_register_1 (.D(Imm), .load(IRLD), .clock(clock_1_out), .Q(n16_bit_register_1_q));
  Multiplexer #(.width(16), .enable("false")) multiplexer_1 (
    .in0(alu_1_out), .in1(Imm), .out(multiplexer_1_out), .sel(MUX));
  Multiplexer #(.select(2), .width(16), .enable("false")) multiplexer_2 (
    .in0(register_bank_1_reg0), .in1(register_bank_1_reg1), .in2(register_bank_1_reg2),
    .in3(register_bank_1_reg3), .out(multiplexer_2_out), .sel(n16_bit_register_1_q[7:6]));
  ALU alu_1 (.in1(multiplexer_2_out), .in2(multiplexer_3_out), .out(alu_1_out), .ALU_SEL(n16_bit_register_1_q[11:8]));
  Multiplexer #(.select(2), .width(16), .enable("false")) multiplexer_3 (
    .in0(register_bank_1_reg0), .in1(register_bank_1_reg1), .in2(register_bank_1_reg2),
    .in3(register_bank_1_reg3), .out(multiplexer_3_out), .sel(n16_bit_register_1_q[3:2]));
  control_unit control_unit_1 (
    .clock(clock_1_out), .irld(IRLD), .pc_inc(PC_INC), .regload(REGLOAD), .mux(MUX), .in_2(Imm));  // open: fetch
  Hex_Digit_Display hex_digit_display_1 (.value(register_bank_1_reg0[11:8]));  // open: dp
  Hex_Digit_Display hex_digit_display_2 (.value(register_bank_1_reg0[15:12]));  // open: dp
  Clock clock_1 (.out(clock_1_out));
  Hex_Digit_Display hex_digit_display_3 (.value(register_bank_1_reg0[7:4]));  // open: dp
  Hex_Digit_Display hex_digit_display_4 (.value(register_bank_1_reg0[3:0]));  // open: dp

  // Notes on the sheet:
  //   contents of rom_1 (hex, n*v repeats v):
  //   4000 75 4001 40 8304 8700 4001 2f 4002 f 8249 8104 8800 4001 c 4002 5f 8149 8541 8404
endmodule

// Register Bank
module register_bank (
  input  clk,
  input  [1:0] REGSEL,
  input  REGLD,
  input  [15:0] D_in,
  output [15:0] reg0,
  output [15:0] reg1,
  output [15:0] reg2,
  output [15:0] reg3
);

  wire and_1_out, and_2_out, and_3_out, and_4_out, demultiplexer_1_out0, demultiplexer_1_out1,
       demultiplexer_1_out2, demultiplexer_1_out3;

  Demultiplexer #(.select(2), .enable("false")) demultiplexer_1 (
    .out0(demultiplexer_1_out0), .out1(demultiplexer_1_out1), .out2(demultiplexer_1_out2),
    .out3(demultiplexer_1_out3), .in(1'b1), .sel(REGSEL));
  and and_1 (and_1_out, demultiplexer_1_out0, REGLD);
  and and_2 (and_2_out, demultiplexer_1_out1, REGLD);
  and and_3 (and_3_out, demultiplexer_1_out2, REGLD);
  and and_4 (and_4_out, demultiplexer_1_out3, REGLD);
  _16_bit_register u_16_bit_register_1 (.D(D_in), .load(and_1_out), .clock(clk), .Q(reg0));
  _16_bit_register u_16_bit_register_2 (.D(D_in), .load(and_2_out), .clock(clk), .Q(reg1));
  _16_bit_register u_16_bit_register_3 (.D(D_in), .load(and_3_out), .clock(clk), .Q(reg2));
  _16_bit_register u_16_bit_register_4 (.D(D_in), .load(and_4_out), .clock(clk), .Q(reg3));
endmodule

module ALU (
  input  [3:0] ALU_SEL,
  input  [15:0] in1,
  input  [15:0] in2,
  output [15:0] out
);

  wire add_out, dec, default_out, inc, inc_dec, not_1_out, not_2_out, not_3_out, not_4_out, not_5_out,
       not_6_out, not_8_out, not_9_out, not_10_out, not_11_out, not_12_out, not_13_out, not_14_out,
       not_15_out, not_16_out, not_17_out, not_19_out, not_20_out, not_21_out, not_22_out, not_23_out,
       not_24_out, not_25_out, sub_out;
  wire [2:0] or_1_out, or_4_out, or_5_out;
  wire [15:0] adder_1_out, and_1_out, multiplexer_1_out, multiplexer_2_out, multiplexer_3_out,
       multiplexer_4_out, not_7_out, or_3_out, subtractor_1_out, xor_1_out;

  Multiplexer #(.width(16), .enable("false")) multiplexer_1 (
    .in0(in2), .in1(16'h1), .out(multiplexer_1_out), .sel(inc_dec));
  not not_1 (not_1_out, ALU_SEL[2]);
  not not_2 (not_2_out, ALU_SEL[1]);
  not not_3 (not_3_out, ALU_SEL[2]);
  not not_4 (not_4_out, ALU_SEL[3]);
  not not_5 (not_5_out, ALU_SEL[3]);
  not not_6 (not_6_out, ALU_SEL[0]);
  and sub (sub_out, not_5_out, not_1_out, not_8_out, ALU_SEL[0]);
  and add (add_out, not_4_out, not_3_out, not_2_out, not_6_out);
  or or_1 (or_1_out[0], inc, add_out);
  or or_2 (or_1_out[1], dec, sub_out);
  Adder #(.width(16)) adder_1 (.a(in1), .b(multiplexer_1_out), .out(adder_1_out));  // open: cin, cout
  Subtractor #(.width(16)) subtractor_1 (.a(in1), .b(multiplexer_1_out), .out(subtractor_1_out));  // open: bin, bout
  assign and_1_out = in1 & multiplexer_1_out;  // AND_Gate and_1, 16 bits wide
  assign or_3_out = in1 | multiplexer_1_out;  // OR_Gate or_3, 16 bits wide
  assign xor_1_out = in1 ^ multiplexer_1_out;  // XOR_Gate xor_1, 16 bits wide
  assign not_7_out = ~in1;  // NOT_Gate not_7, 16 bits wide
  not not_8 (not_8_out, ALU_SEL[1]);
  not not_9 (not_9_out, ALU_SEL[0]);
  not not_10 (not_10_out, ALU_SEL[2]);
  not not_11 (not_11_out, ALU_SEL[3]);
  and and_2 (or_1_out[2], not_11_out, not_10_out, ALU_SEL[1], not_9_out);
  Multiplexer #(.select(3), .width(16), .enable("false")) multiplexer_2 (
    .in1(adder_1_out), .in2(subtractor_1_out), .in4(and_1_out), .out(multiplexer_2_out), .sel(or_1_out));  // open: in0, in3, in5, in6, in7
  Multiplexer #(.select(3), .width(16), .enable("false")) multiplexer_3 (
    .in1(or_3_out), .in2(xor_1_out), .in4(not_7_out), .out(multiplexer_3_out), .sel(or_4_out));  // open: in0, in3, in5, in6, in7
  not not_12 (not_12_out, ALU_SEL[3]);
  not not_13 (not_13_out, ALU_SEL[3]);
  not not_14 (not_14_out, ALU_SEL[2]);
  and or_4 (or_4_out[0], not_12_out, not_14_out, ALU_SEL[1], ALU_SEL[0]);
  or or_5 (or_5_out[0], sub_out, add_out, or_1_out[2], inc_dec);
  not not_15 (not_15_out, ALU_SEL[0]);
  not not_16 (not_16_out, ALU_SEL[1]);
  not not_17 (not_17_out, ALU_SEL[3]);
  and not_18 (or_4_out[2], not_17_out, ALU_SEL[2], not_19_out, ALU_SEL[0]);
  and xor_2 (or_4_out[1], not_13_out, ALU_SEL[2], not_16_out, not_15_out);
  not not_19 (not_19_out, ALU_SEL[1]);
  not not_20 (not_20_out, ALU_SEL[0]);
  not not_21 (not_21_out, ALU_SEL[3]);
  and mov (or_5_out[2], not_21_out, ALU_SEL[2], ALU_SEL[1], not_20_out);
  or or_6 (or_5_out[1], or_4_out[0], or_4_out[1], or_4_out[2]);
  Multiplexer #(.select(3), .width(16), .enable("false")) multiplexer_4 (
    .in1(multiplexer_2_out), .in2(multiplexer_3_out), .in4(in1), .out(multiplexer_4_out), .sel(or_5_out));  // open: in0, in3, in5, in6, in7
  not not_22 (not_22_out, ALU_SEL[3]);
  and u_inc (inc, not_22_out, ALU_SEL[2], ALU_SEL[1], ALU_SEL[0]);
  or or_7 (inc_dec, inc, dec);
  Multiplexer #(.width(16), .enable("false")) multiplexer_5 (
    .in0(multiplexer_4_out), .in1({16{1'b0}}), .out(out), .sel(default_out));
  not not_23 (not_23_out, ALU_SEL[1]);
  not not_24 (not_24_out, ALU_SEL[2]);
  not not_25 (not_25_out, ALU_SEL[0]);
  and \default  (default_out, ALU_SEL[3], ALU_SEL[2], ALU_SEL[1], ALU_SEL[0]);
  and u_dec (dec, ALU_SEL[3], not_24_out, not_23_out, not_25_out);
endmodule

// PC
module pc (
  input  clk,
  input  PC_INC,
  output [7:0] out
);

  wire [7:0] adder_1_out;

  Adder adder_1 (.a(out), .b(8'h1), .out(adder_1_out));  // open: cin, cout
  _8_bit_register pc_Register (.clk(clk), .D(adder_1_out), .load(PC_INC), .Q(out));
endmodule

// Control Unit
module control_unit (
  input  clock,
  input  [15:0] in_2,
  output fetch,
  output irld,
  output pc_inc,
  output regload,
  output mux
);

  wire not_1_out, not_2_out;
  wire [1:0] multiplexer_1_out, s_r_ff_1_q;

  Multiplexer #(.width(2), .enable("false")) multiplexer_1 (
    .in0(2'b00), .in1(in_2[15:14]), .out(multiplexer_1_out), .sel(fetch));
  not not_1 (not_1_out, multiplexer_1_out[0]);
  not not_2 (not_2_out, multiplexer_1_out[1]);
  S_R_Flip_Flop s_r_ff_1 (
    .S(multiplexer_1_out[0]), .clk(clock), .R(not_1_out), .Q(s_r_ff_1_q[0]), .en(1'b1));  // open: Qn, preset, reset
  S_R_Flip_Flop s_r_ff_2 (
    .S(multiplexer_1_out[1]), .clk(clock), .R(not_2_out), .Q(s_r_ff_1_q[1]), .en(1'b1));  // open: Qn, preset, reset
  ROM #(.addrWidth(2), .dataWidth(5)) rom_1 (
    .addr(s_r_ff_1_q), .data({mux, regload, pc_inc, irld, fetch}));  // open: sel

  // Notes on the sheet:
  //   contents of rom_1 (hex, n*v repeats v):
  //   7 1c 8
endmodule

// IR
module _16_bit_register (
  input  [15:0] D,
  input  load,
  input  clock,
  output [15:0] Q
);

  wire not_1_out, not_2_out, not_3_out, not_4_out, not_5_out, not_6_out, not_7_out, not_8_out, not_9_out,
       not_10_out, not_11_out, not_12_out, not_13_out, not_14_out, not_15_out, not_16_out;

  not not_1 (not_1_out, D[2]);
  not not_2 (not_2_out, D[6]);
  not not_3 (not_3_out, D[5]);
  not not_4 (not_4_out, D[3]);
  not not_5 (not_5_out, D[0]);
  not not_6 (not_6_out, D[1]);
  not not_7 (not_7_out, D[4]);
  not not_8 (not_8_out, D[7]);
  not not_9 (not_9_out, D[12]);
  not not_10 (not_10_out, D[11]);
  not not_11 (not_11_out, D[14]);
  not not_12 (not_12_out, D[13]);
  not not_13 (not_13_out, D[8]);
  not not_14 (not_14_out, D[9]);
  not not_15 (not_15_out, D[10]);
  not not_16 (not_16_out, D[15]);
  S_R_Flip_Flop #(.trigger("falling")) s_r_ff_1 (
    .S(D[1]), .clk(clock), .R(not_6_out), .Q(Q[1]), .en(load));  // open: Qn, preset, reset
  S_R_Flip_Flop #(.trigger("falling")) s_r_ff_2 (
    .S(D[3]), .clk(clock), .R(not_4_out), .Q(Q[3]), .en(load));  // open: Qn, preset, reset
  S_R_Flip_Flop #(.trigger("falling")) s_r_ff_3 (
    .S(D[5]), .clk(clock), .R(not_3_out), .Q(Q[5]), .en(load));  // open: Qn, preset, reset
  S_R_Flip_Flop #(.trigger("falling")) s_r_ff_4 (
    .S(D[7]), .clk(clock), .R(not_8_out), .Q(Q[7]), .en(load));  // open: Qn, preset, reset
  S_R_Flip_Flop #(.trigger("falling")) s_r_ff_5 (
    .S(D[9]), .clk(clock), .R(not_14_out), .Q(Q[9]), .en(load));  // open: Qn, preset, reset
  S_R_Flip_Flop #(.trigger("falling")) s_r_ff_6 (
    .S(D[11]), .clk(clock), .R(not_10_out), .Q(Q[11]), .en(load));  // open: Qn, preset, reset
  S_R_Flip_Flop #(.trigger("falling")) s_r_ff_7 (
    .S(D[13]), .clk(clock), .R(not_12_out), .Q(Q[13]), .en(load));  // open: Qn, preset, reset
  S_R_Flip_Flop #(.trigger("falling")) s_r_ff_8 (
    .S(D[15]), .clk(clock), .R(not_16_out), .Q(Q[15]), .en(load));  // open: Qn, preset, reset
  S_R_Flip_Flop #(.trigger("falling")) s_r_ff_9 (
    .S(D[0]), .clk(clock), .R(not_5_out), .Q(Q[0]), .en(load));  // open: Qn, preset, reset
  S_R_Flip_Flop #(.trigger("falling")) s_r_ff_10 (
    .S(D[2]), .clk(clock), .R(not_1_out), .Q(Q[2]), .en(load));  // open: Qn, preset, reset
  S_R_Flip_Flop #(.trigger("falling")) s_r_ff_11 (
    .S(D[4]), .clk(clock), .R(not_7_out), .Q(Q[4]), .en(load));  // open: Qn, preset, reset
  S_R_Flip_Flop #(.trigger("falling")) s_r_ff_12 (
    .S(D[6]), .clk(clock), .R(not_2_out), .Q(Q[6]), .en(load));  // open: Qn, preset, reset
  S_R_Flip_Flop #(.trigger("falling")) s_r_ff_13 (
    .S(D[8]), .clk(clock), .R(not_13_out), .Q(Q[8]), .en(load));  // open: Qn, preset, reset
  S_R_Flip_Flop #(.trigger("falling")) s_r_ff_14 (
    .S(D[10]), .clk(clock), .R(not_15_out), .Q(Q[10]), .en(load));  // open: Qn, preset, reset
  S_R_Flip_Flop #(.trigger("falling")) s_r_ff_15 (
    .S(D[12]), .clk(clock), .R(not_9_out), .Q(Q[12]), .en(load));  // open: Qn, preset, reset
  S_R_Flip_Flop #(.trigger("falling")) s_r_ff_16 (
    .S(D[14]), .clk(clock), .R(not_11_out), .Q(Q[14]), .en(load));  // open: Qn, preset, reset

  // Other names for the same wires on the sheet: a[8:0] = D[8:0]; b[6:0] = D[15:9]
endmodule

module _8_bit_register (
  input  clk,
  input  [7:0] D,
  input  load,
  output [7:0] Q
);

  wire not_1_out, not_2_out, not_3_out, not_4_out, not_5_out, not_6_out, not_7_out, not_8_out;

  not not_1 (not_1_out, D[0]);
  not not_2 (not_2_out, D[1]);
  not not_3 (not_3_out, D[2]);
  not not_4 (not_4_out, D[3]);
  not not_5 (not_5_out, D[4]);
  not not_6 (not_6_out, D[5]);
  not not_7 (not_7_out, D[6]);
  not not_8 (not_8_out, D[7]);
  S_R_Flip_Flop s_r_ff_1 (.S(D[0]), .clk(clk), .R(not_1_out), .Q(Q[0]), .en(load));  // open: Qn, preset, reset
  S_R_Flip_Flop s_r_ff_2 (.S(D[1]), .clk(clk), .R(not_2_out), .Q(Q[1]), .en(load));  // open: Qn, preset, reset
  S_R_Flip_Flop s_r_ff_3 (.S(D[2]), .clk(clk), .R(not_3_out), .Q(Q[2]), .en(load));  // open: Qn, preset, reset
  S_R_Flip_Flop s_r_ff_4 (.S(D[3]), .clk(clk), .R(not_4_out), .Q(Q[3]), .en(load));  // open: Qn, preset, reset
  S_R_Flip_Flop s_r_ff_5 (.S(D[4]), .clk(clk), .R(not_5_out), .Q(Q[4]), .en(load));  // open: Qn, preset, reset
  S_R_Flip_Flop s_r_ff_6 (.S(D[5]), .clk(clk), .R(not_6_out), .Q(Q[5]), .en(load));  // open: Qn, preset, reset
  S_R_Flip_Flop s_r_ff_7 (.S(D[6]), .clk(clk), .R(not_7_out), .Q(Q[6]), .en(load));  // open: Qn, preset, reset
  S_R_Flip_Flop s_r_ff_8 (.S(D[7]), .clk(clk), .R(not_8_out), .Q(Q[7]), .en(load));  // open: Qn, preset, reset
endmodule
