// Logisim project Mammal.circ as structural Verilog: 15 circuits, main circuit main
module main (
  input  [15:0] in_1
);

  wire _777_out, AFA_out, and_1_out, BFA_out, BFC_out, clock_1_int, CLOCK_2_out, cpu_1_intack, cpu_1_memld,
       not_1_out, not_2_out, not_3_out, not_4_out, not_5_out, not_6_out, not_7_out, not_8_out, not_9_out,
       not_10_out, not_11_out, not_12_out, not_13_out, not_14_out, or_1_out, pic_1_int_out, pop_1_dout,
       READY_out;
  wire [0:0] pic_1_int_addr;
  wire [1:0] priority_encoder_1_out;
  wire [3:0] n16_bit_register_1_q;
  wire [11:0] cpu_1_addr;
  wire [15:0] clock_1_out, controlled_buffer_1_out, cpu_1_dout, io_device_1_d_out, Memory_Output,
       multiplexer_1_out, multiplexer_2_out, multiplexer_3_out, multiplexer_4_out, n16_bit_register_2_q;
  wire [15:4] n16_bit_register_1_q_2;

  clock clock_1 (.clk(CLOCK_2_out), .INT(clock_1_int), .out(clock_1_out));
  PIC pic_1 (
    .INT_in(clock_1_int), .INT_addr(pic_1_int_addr[0]), .INT_out(pic_1_int_out), .INTACK(cpu_1_intack),
    .clk(CLOCK_2_out));
  Button READY (.out(READY_out));
  IO_device io_device_1 (
    .d_in(in_1), .d_out(io_device_1_d_out), .ready(READY_out), .device_addr(AFA_out), .a0(cpu_1_addr[0]));
  and and_1 (and_1_out, not_1_out, not_2_out);
  not not_1 (not_1_out, AFA_out);
  not not_2 (not_2_out, _777_out);
  Multiplexer #(.select(2), .width(16), .enable("false")) multiplexer_1 (
    .in0({16{1'b0}}), .in1(Memory_Output), .in2(io_device_1_d_out), .in3(clock_1_out),
    .out(multiplexer_1_out), .sel(priority_encoder_1_out));
  Priority_Encoder #(.select(2)) priority_encoder_1 (
    .in0(1'b1), .in1(and_1_out), .in2(AFA_out), .in3(_777_out), .out(priority_encoder_1_out));
  and AFA (AFA_out, cpu_1_addr[11], not_4_out, cpu_1_addr[9], not_3_out, cpu_1_addr[7], cpu_1_addr[6], cpu_1_addr[5], cpu_1_addr[4], cpu_1_addr[3], not_6_out, cpu_1_addr[1]);
  not not_3 (not_3_out, cpu_1_addr[8]);
  not not_4 (not_4_out, cpu_1_addr[10]);
  not not_5 (not_5_out, cpu_1_addr[11]);
  Multiplexer #(.width(16), .enable("false")) multiplexer_2 (
    .in0(multiplexer_1_out), .in1({{15{1'b0}}, pic_1_int_addr[0]}), .out(multiplexer_2_out),
    .sel(cpu_1_intack));
  POP pop_1 (.Din(multiplexer_1_out), .clk(CLOCK_2_out), .Dout(pop_1_dout));
  not not_6 (not_6_out, cpu_1_addr[2]);
  and _777 (_777_out, not_5_out, cpu_1_addr[10], cpu_1_addr[9], cpu_1_addr[8], not_8_out, cpu_1_addr[6], cpu_1_addr[5], cpu_1_addr[4], not_7_out, cpu_1_addr[2], cpu_1_addr[1], cpu_1_addr[0]);
  not not_7 (not_7_out, cpu_1_addr[3]);
  not not_8 (not_8_out, cpu_1_addr[7]);
  CPU cpu_1 (
    .Din(multiplexer_2_out), .Dout(cpu_1_dout), .Addr(cpu_1_addr), .CLOCK(CLOCK_2_out), .MEMLD(cpu_1_memld),
    .INTACK(cpu_1_intack), .INT(pic_1_int_out));
  Multiplexer #(.width(16), .enable("false")) multiplexer_3 (
    .in0(multiplexer_4_out), .in1({16{1'b0}}), .out(multiplexer_3_out), .sel(pop_1_dout));
  Multiplexer #(.width(16), .enable("false")) multiplexer_4 (
    .in0(cpu_1_dout), .in1(io_device_1_d_out), .out(multiplexer_4_out), .sel(AFA_out));
  or or_1 (or_1_out, cpu_1_memld, pop_1_dout, AFA_out);
  RAM #(.addrWidth(12), .dataWidth(16), .bus("separate")) ram_1 (
    .addr(cpu_1_addr), .din(multiplexer_3_out), .data(Memory_Output), .str(or_1_out), .clk(CLOCK_2_out));  // open: sel, ld, clr
  not not_9 (not_9_out, cpu_1_addr[2]);
  not not_10 (not_10_out, cpu_1_addr[0]);
  assign controlled_buffer_1_out = BFA_out ? Memory_Output : 16'bz;  // Controlled_Buffer controlled_buffer_1
  and BFA (BFA_out, not_10_out, cpu_1_addr[1], not_9_out, cpu_1_addr[3], cpu_1_addr[4], cpu_1_addr[5], cpu_1_addr[6], cpu_1_addr[7], cpu_1_addr[8], cpu_1_addr[9], not_11_out, cpu_1_addr[11]);
  not not_11 (not_11_out, cpu_1_addr[10]);
  _16_bit_register u_16_bit_register_1 (
    .D(controlled_buffer_1_out), .load(BFA_out), .clock(CLOCK_2_out),
    .Q({n16_bit_register_1_q_2, n16_bit_register_1_q}));
  _16_bit_register u_16_bit_register_2 (
    .D(Memory_Output), .load(BFC_out), .clock(CLOCK_2_out), .Q(n16_bit_register_2_q));
  and BFC (BFC_out, not_12_out, not_13_out, cpu_1_addr[2], cpu_1_addr[3], cpu_1_addr[4], cpu_1_addr[5], cpu_1_addr[6], cpu_1_addr[7], cpu_1_addr[8], cpu_1_addr[9], not_14_out, cpu_1_addr[11]);
  not not_12 (not_12_out, cpu_1_addr[0]);
  not not_13 (not_13_out, cpu_1_addr[1]);
  Hex_Digit_Display hex_digit_display_1 (.value(n16_bit_register_1_q_2[15:12]));  // open: dp
  Hex_Digit_Display hex_digit_display_2 (.value(n16_bit_register_1_q_2[11:8]));  // open: dp
  not not_14 (not_14_out, cpu_1_addr[10]);
  Clock CLOCK_2 (.out(CLOCK_2_out));
  Hex_Digit_Display hex_digit_display_3 (.value(n16_bit_register_1_q_2[7:4]));  // open: dp
  Hex_Digit_Display hex_digit_display_4 (.value(n16_bit_register_1_q));  // open: dp
  Hex_Digit_Display hex_digit_display_5 (.value(n16_bit_register_2_q[15:12]));  // open: dp
  Hex_Digit_Display hex_digit_display_6 (.value(n16_bit_register_2_q[11:8]));  // open: dp
  Hex_Digit_Display hex_digit_display_7 (.value(n16_bit_register_2_q[3:0]));  // open: dp
  Hex_Digit_Display hex_digit_display_8 (.value(n16_bit_register_2_q[7:4]));  // open: dp

  // Notes on the sheet:
  //   add2number
  //   clock
  //   ADD TWO NUMBER
  //   CLOCK
endmodule

// IO Device
module IO_device (
  input  [15:0] d_in,
  input  ready,
  input  device_addr,
  input  a0,
  output [15:0] d_out
);

  wire and_1_out, not_1_out;
  wire [2:2] register_2_q;
  wire [15:0] register_1_q;

  Register #(.width(16)) register_1 (.D(d_in), .en(1'b1), .Q(register_1_q), .clk(register_2_q[2]));  // open: clr
  Register #(.width(1)) register_2 (.D(1'b1), .en(1'b1), .Q(register_2_q[2]), .clk(ready), .clr(and_1_out));
  and and_1 (and_1_out, device_addr, not_1_out);
  not not_1 (not_1_out, a0);
  Multiplexer #(.width(16), .enable("false")) multiplexer_1 (
    .in0(register_1_q), .in1({{13{1'b0}}, register_2_q[2], 2'b00}), .out(d_out), .sel(a0));

  // Notes on the sheet:
  //   Whenever a0=0, CPU gets the DATA register
endmodule

module CPU (
  input  CLOCK,
  input  [15:0] Din,
  input  INT,
  output [15:0] Dout,
  output [11:0] Addr,
  output MEMLD,
  output INTACK
);

  wire alu_1_zf, and_1_out, CLI, FLAGLD, IF, INTLD, IRLD, MUX, not_1_out, not_2_out, not_3_out, not_4_out,
       PC_INC, PC_LD, PC_MUX, register_1_q, REGLD, SPDEC, SPINC, STI, ZF, ZFLD;
  wire [1:0] ADDRMUX, DATAMUX;
  wire [3:0] multiplexer_5_out_2, multiplexer_7_out_2, register_bank_1_reg7_stack_register_2;
  wire [11:0] adder_1_out, adder_2_out, bit_extender_1_out, INTADDR, multiplexer_4_out, multiplexer_5_out,
       multiplexer_7_out, pc_1_out, register_bank_1_reg7_stack_register;
  wire [15:0] alu_1_out, INTREG, IR_Cable, multiplexer_1_out, register_bank_1_reg0, register_bank_1_reg1,
       register_bank_1_reg2, register_bank_1_reg3, register_bank_1_reg4, register_bank_1_reg5, src2,
       subtractor_1_out;

  Register #(.width(1)) register_1 (.D(INT), .en(1'b1), .Q(register_1_q), .clk(CLOCK));  // open: clr
  and and_1 (and_1_out, 1'b1, not_2_out, not_1_out, not_3_out, not_4_out);
  not not_1 (not_1_out, Din[14]);
  not not_2 (not_2_out, Din[15]);
  not not_3 (not_3_out, Din[13]);
  Multiplexer #(.width(16), .enable("false")) multiplexer_1 (
    .in0({4'b0000, pc_1_out}), .in1(subtractor_1_out), .out(multiplexer_1_out), .sel(register_1_q));
  Subtractor #(.width(16)) subtractor_1 (
    .a({4'b0000, pc_1_out}), .b(16'h1), .out(subtractor_1_out));  // open: bin, bout
  not not_4 (not_4_out, Din[12]);
  Multiplexer #(.select(2), .width(12), .enable("false")) multiplexer_2 (
    .in0(pc_1_out), .in1(multiplexer_7_out), .in2(register_bank_1_reg7_stack_register), .in3(INTADDR),
    .out(Addr), .sel(ADDRMUX));
  pc pc_1 (.out(pc_1_out), .clk(CLOCK), .PC_INC(PC_INC), .\input (multiplexer_4_out), .PC_LD(PC_LD));
  Adder #(.width(12)) adder_1 (.a(pc_1_out), .b(IR_Cable[11:0]), .out(adder_1_out));  // open: cin, cout
  Multiplexer #(.select(2), .width(16), .enable("false")) multiplexer_3 (
    .in0(multiplexer_1_out), .in1(src2), .in2(INTREG), .out(Dout), .sel(DATAMUX));  // open: in3
  Multiplexer #(.width(12), .enable("false")) multiplexer_4 (
    .in0(adder_1_out), .in1(multiplexer_5_out), .out(multiplexer_4_out), .sel(PC_MUX));
  register_bank register_bank_1 (
    .D_in({multiplexer_5_out_2, multiplexer_5_out}), .REGSEL(IR_Cable[2:0]), .reg0(register_bank_1_reg0),
    .reg2(register_bank_1_reg2), .REGLD(REGLD), .reg1(register_bank_1_reg1), .reg3(register_bank_1_reg3),
    .clk(CLOCK), .reg4(register_bank_1_reg4), .reg5(register_bank_1_reg5), .reg6(INTREG),
    .reg7_Stack_Register({register_bank_1_reg7_stack_register_2, register_bank_1_reg7_stack_register}),
    .SPINC(SPINC), .SPDEC(SPDEC), .IF(IF), .FLAGLD(FLAGLD), .ZFLD(ZFLD), .STI(STI), .CLI(CLI), .ZF(ZF));
  _16_bit_register u_16_bit_register_1 (.D(Din), .load(IRLD), .clock(CLOCK), .Q(IR_Cable));
  Multiplexer #(.width(16), .enable("false")) multiplexer_5 (
    .in0(Din), .in1(alu_1_out), .out({multiplexer_5_out_2, multiplexer_5_out}), .sel(MUX));
  Multiplexer #(.select(3), .width(16), .enable("false")) multiplexer_6 (
    .in0(register_bank_1_reg0), .in1(register_bank_1_reg1), .in2(register_bank_1_reg2),
    .in3(register_bank_1_reg3), .in4(register_bank_1_reg4), .in5(register_bank_1_reg5), .in6(INTREG),
    .in7({register_bank_1_reg7_stack_register_2, register_bank_1_reg7_stack_register}), .out(src2),
    .sel(IR_Cable[8:6]));
  Register #(.width(1)) register_2 (.D(alu_1_zf), .en(ZFLD), .Q(ZF), .clk(CLOCK));  // open: clr
  Multiplexer #(.select(3), .width(16), .enable("false")) multiplexer_7 (
    .in0(register_bank_1_reg0), .in1(register_bank_1_reg1), .in2(register_bank_1_reg2),
    .in3(register_bank_1_reg3), .in4(register_bank_1_reg4), .in5(register_bank_1_reg5), .in6(INTREG),
    .in7({register_bank_1_reg7_stack_register_2, register_bank_1_reg7_stack_register}),
    .out({multiplexer_7_out_2, multiplexer_7_out}), .sel(IR_Cable[5:3]));
  ALU alu_1 (
    .in1({multiplexer_7_out_2, multiplexer_7_out}), .in2(src2), .ALU_EXTRA(IR_Cable[8:6]),
    .ALUSEL(IR_Cable[11:9]), .out(alu_1_out), .ZF(alu_1_zf));
  control_unit control_unit_1 (
    .clock(CLOCK), .opcode(Din), .zf(ZF), .MUX(MUX), .PCLD(PC_LD), .PCINC(PC_INC), .IRLD(IRLD),
    .REGLD(REGLD), .MEMLD(MEMLD), .ZFLD(ZFLD), .SPINC(SPINC), .SPDEC(SPDEC), .PCMUX(PC_MUX), .INTACK(INTACK),
    .INTLD(INTLD), .FLAGLD(FLAGLD), .STI(STI), .CLI(CLI), .IF(IF), .INT(INT), .ADDRMUX(ADDRMUX),
    .DATAMUX(DATAMUX));
  assign bit_extender_1_out = {{9{1'b0}}, Din[2:0]};  // Bit_Extender bit_extender_1
  Register #(.width(12), .trigger("falling")) register_3 (
    .D(adder_2_out), .en(INTLD), .Q(INTADDR), .clk(CLOCK));  // open: clr
  Adder #(.width(12)) adder_2 (.a(bit_extender_1_out), .b(12'h7f0), .out(adder_2_out));  // open: cin, cout

  // Other names for the same wires on the sheet: Imm[15:0] = Din

  // Notes on the sheet:
  //   DataMux=1 ; MEM[sp]=PC (call operation)
  //   pc = ir + pc (jump operation)
  //   mem[src2] = src1 (LOAD & STORE)
  //   pc is set to stack register's content!
  //   Source #2
  //   Source #1
endmodule

// Control Unit
module control_unit (
  input  IF,
  input  INT,
  input  clock,
  input  zf,
  input  [15:0] opcode,
  output MUX,
  output PCLD,
  output PCINC,
  output IRLD,
  output REGLD,
  output MEMLD,
  output ZFLD,
  output SPINC,
  output SPDEC,
  output PCMUX,
  output INTACK,
  output INTLD,
  output FLAGLD,
  output [1:0] ADDRMUX,
  output [1:0] DATAMUX,
  output STI,
  output CLI
);

  wire and_1_out, and_3_out, fetch, not_1_out, not_2_out, not_3_out, not_4_out, not_5_out, not_6_out,
       not_7_out, not_8_out, not_9_out, not_10_out, not_11_out, not_12_out, not_13_out, not_14_out,
       not_15_out, not_16_out, not_17_out, not_18_out, not_19_out, not_20_out, not_21_out, not_22_out,
       not_23_out, not_24_out, priority_encoder_1_p3, priority_encoder_1_p4, priority_encoder_1_p5,
       priority_encoder_1_p6, priority_encoder_1_p7, priority_encoder_1_p8;
  wire [1:1] and_2_out;
  wire [2:0] priority_encoder_1_p1;
  wire [3:0] multiplexer_3_out;
  wire [4:0] multiplexer_1_out, multiplexer_2_out, multiplexer_4_out, register_1_q;
  wire [18:2] rom_1_data;

  Multiplexer #(.select(3), .width(5), .enable("false")) multiplexer_1 (
    .in0({5{1'b0}}), .in1(5'b01100), .in2(5'b01101), .in3(5'b10010), .in4(5'b10011), .in5(5'b10100),
    .in6(5'b10101), .out(multiplexer_1_out), .sel(priority_encoder_1_p1));  // open: in7
  // Priority_Encoder priority_encoder_1: pin names not known; wires that end beside it: priority_encoder_1_p1, 1'b1, priority_encoder_1_p3, priority_encoder_1_p4, priority_encoder_1_p5, priority_encoder_1_p6, priority_encoder_1_p7, priority_encoder_1_p8
  not not_1 (not_1_out, multiplexer_1_out[0]);
  not not_2 (not_2_out, multiplexer_1_out[1]);
  not not_3 (not_3_out, multiplexer_1_out[2]);
  and and_1 (and_1_out, not_1_out, not_2_out, not_3_out, not_4_out, not_5_out);
  not not_4 (not_4_out, multiplexer_1_out[3]);
  not not_5 (not_5_out, multiplexer_1_out[4]);
  and and_2 (and_2_out[1], not_6_out, opcode[14], not_7_out, opcode[12]);
  not not_6 (not_6_out, opcode[15]);
  not not_7 (not_7_out, opcode[13]);
  and _0x9 (priority_encoder_1_p3, register_1_q[0], not_8_out, not_9_out, register_1_q[3], not_10_out);
  and _0xb (priority_encoder_1_p4, register_1_q[0], register_1_q[1], not_11_out, register_1_q[3], not_12_out);
  Multiplexer #(.width(5), .enable("false")) multiplexer_2 (
    .in0(multiplexer_1_out), .in1({1'b0, multiplexer_3_out}), .out(multiplexer_2_out), .sel(fetch));
  Multiplexer #(.select(2), .width(4), .enable("false")) multiplexer_3 (
    .in0(opcode[15:12]), .in1(opcode[15:12]), .in2(4'b0000), .in3(4'b0100), .out(multiplexer_3_out),
    .sel({and_2_out[1], zf}));
  not not_8 (not_8_out, register_1_q[1]);
  not not_9 (not_9_out, register_1_q[2]);
  not not_10 (not_10_out, register_1_q[4]);
  not not_11 (not_11_out, register_1_q[2]);
  not not_12 (not_12_out, register_1_q[4]);
  and and_3 (and_3_out, and_1_out, IF, INT);
  Multiplexer #(.width(5), .enable("false")) multiplexer_4 (
    .in0(multiplexer_2_out), .in1(5'b10000), .out(multiplexer_4_out), .sel(and_3_out));
  and _0x10 (priority_encoder_1_p5, not_13_out, not_14_out, not_15_out, not_16_out, register_1_q[4]);
  and _0x6 (priority_encoder_1_p6, not_17_out, register_1_q[1], register_1_q[2], not_18_out, not_19_out);
  addr_mux addr_mux_1 (.in(register_1_q), .out(ADDRMUX));
  not not_13 (not_13_out, register_1_q[0]);
  not not_14 (not_14_out, register_1_q[1]);
  not not_15 (not_15_out, register_1_q[2]);
  not not_16 (not_16_out, register_1_q[3]);
  not not_17 (not_17_out, register_1_q[0]);
  not not_18 (not_18_out, register_1_q[3]);
  not not_19 (not_19_out, register_1_q[4]);
  Register #(.width(5)) register_1 (.D(multiplexer_4_out), .en(1'b1), .Q(register_1_q), .clk(clock));  // open: clr
  and _0x12 (priority_encoder_1_p7, not_20_out, register_1_q[1], not_21_out, not_22_out, register_1_q[4]);
  and _0x13 (priority_encoder_1_p8, register_1_q[0], register_1_q[1], not_23_out, not_24_out, register_1_q[4]);
  data_mux data_mux_1 (.in(register_1_q), .out(DATAMUX));
  not not_20 (not_20_out, register_1_q[0]);
  not not_21 (not_21_out, register_1_q[2]);
  not not_22 (not_22_out, register_1_q[3]);
  not not_23 (not_23_out, register_1_q[2]);
  not not_24 (not_24_out, register_1_q[3]);
  ROM #(.addrWidth(5), .dataWidth(19)) rom_1 (
    .addr(register_1_q),
    .data({rom_1_data[18], CLI, STI, FLAGLD, INTLD, INTACK, rom_1_data[12], PCMUX, SPDEC, SPINC, ZFLD, MEMLD, REGLD, IRLD, PCINC, PCLD, rom_1_data[2], MUX, fetch}));  // open: sel

  // Notes on the sheet:
  //   contents of rom_1 (hex, n*v repeats v):
  //   31 50 44 1084 8 8 200 142 1484 200 48c 200 44 a0c 10000 20000 648c 200 21484 8204 80c 80c
  //   Next Line
  //   Address Mux
  //   Data Mux
endmodule

// Register Bank
module register_bank (
  input  clk,
  input  [2:0] REGSEL,
  input  STI,
  input  CLI,
  input  ZF,
  input  ZFLD,
  input  FLAGLD,
  input  SPINC,
  input  SPDEC,
  input  REGLD,
  input  [15:0] D_in,
  output [15:0] reg0,
  output [15:0] reg1,
  output [15:0] reg2,
  output [15:0] reg3,
  output [15:0] reg4,
  output [15:0] reg5,
  output [15:0] reg6,
  output IF,
  output [15:0] reg7_Stack_Register
);

  wire and_1_out, and_2_out, and_3_out, and_4_out, and_5_out, and_6_out, and_7_out, and_8_out,
       demultiplexer_1_out0, demultiplexer_1_out1, demultiplexer_1_out2, demultiplexer_1_out3,
       demultiplexer_1_out4, demultiplexer_1_out5, demultiplexer_1_out6, demultiplexer_1_out7, or_1_out,
       or_2_out;
  wire [15:0] multiplexer_1_out;

  Demultiplexer #(.select(3), .enable("false")) demultiplexer_1 (
    .out0(demultiplexer_1_out0), .out1(demultiplexer_1_out1), .out2(demultiplexer_1_out2),
    .out3(demultiplexer_1_out3), .out4(demultiplexer_1_out4), .out5(demultiplexer_1_out5),
    .out6(demultiplexer_1_out6), .out7(demultiplexer_1_out7), .in(1'b1), .sel(REGSEL));
  and and_1 (and_1_out, demultiplexer_1_out0, REGLD);
  and and_2 (and_2_out, demultiplexer_1_out1, REGLD);
  and and_3 (and_3_out, demultiplexer_1_out2, REGLD);
  and and_4 (and_4_out, demultiplexer_1_out3, REGLD);
  and and_5 (and_5_out, demultiplexer_1_out4, REGLD);
  and and_6 (and_6_out, demultiplexer_1_out5, REGLD);
  and and_7 (and_7_out, demultiplexer_1_out6, REGLD);
  and and_8 (and_8_out, demultiplexer_1_out7, REGLD);
  _16_bit_register u_16_bit_register_1 (.D(D_in), .load(and_1_out), .clock(clk), .Q(reg0));
  _16_bit_register u_16_bit_register_2 (.D(D_in), .load(and_2_out), .clock(clk), .Q(reg1));
  _16_bit_register u_16_bit_register_3 (.D(D_in), .load(and_3_out), .clock(clk), .Q(reg2));
  _16_bit_register u_16_bit_register_4 (.D(D_in), .load(and_4_out), .clock(clk), .Q(reg3));
  _16_bit_register u_16_bit_register_5 (.D(D_in), .load(and_5_out), .clock(clk), .Q(reg4));
  _16_bit_register u_16_bit_register_6 (.D(D_in), .load(and_6_out), .clock(clk), .Q(reg5));
  Multiplexer #(.width(16), .enable("false")) multiplexer_1 (
    .in0(reg6), .in1(D_in), .out(multiplexer_1_out), .sel(and_7_out));
  or or_1 (or_1_out, SPDEC, and_8_out);
  or or_2 (or_2_out, SPINC, SPDEC);
  _16_bit_register u_16_bit_register_7 ();  // open: D, load, clock, Q
  Counter #(.width(16), .max('hffff)) counter_1 (
    .load(or_1_out), .D(D_in), .count(or_2_out), .Q(reg7_Stack_Register), .clk(clk));  // open: carry, clr
  interrupt_register interrupt_register_1 (
    .in(multiplexer_1_out), .IF(IF), .out(reg6), .sti(STI), .cli(CLI), .clk(clk), .ZF(ZF), .ZFLD(ZFLD),
    .FLAGLD(FLAGLD), .REGLD(and_7_out));
endmodule

// CLOCK
module clock (
  input  clk,
  output [15:0] out,
  output INT
);

  wire comparator_1_gt;
  wire [15:0] adder_1_out, adder_2_out, multiplexer_1_out, register_1_q;

  Adder #(.width(16)) adder_1 (.a(16'h1), .b(register_1_q), .out(adder_1_out));  // open: cin, cout
  Register #(.width(16)) register_1 (.D(adder_1_out), .en(1'b1), .Q(register_1_q), .clk(clk), .clr(comparator_1_gt));
  Comparator #(.width(16)) comparator_1 (.a(register_1_q), .b(16'h190), .gt(comparator_1_gt), .eq(INT));  // open: lt
  Adder #(.width(16)) adder_2 (.a(out), .b(16'h1), .out(adder_2_out));  // open: cin, cout
  Multiplexer #(.width(16), .enable("false")) multiplexer_1 (
    .in0(out), .in1(adder_2_out), .out(multiplexer_1_out), .sel(INT));
  Register #(.width(16)) register_2 (.D(multiplexer_1_out), .en(1'b1), .Q(out), .clk(clk));  // open: clr

  // Notes on the sheet:
  //   0.001 kHz = 1 sec
endmodule

module PIC (
  input  INT_in,
  input  INTACK,
  input  clk,
  output INT_addr,
  output INT_out
);

  wire priority_encoder_1_out, register_1_q;

  Priority_Encoder #(.select(1)) priority_encoder_1 (
    .in0(1'b1), .in1(INT_in), .out(priority_encoder_1_out));  // open: gs, en_out, en_in
  Register #(.width(1), .trigger("falling")) register_1 (.D(INTACK), .Q(register_1_q), .clk(clk));  // open: en, clr
  Register #(.width(1), .trigger("falling")) register_2 (
    .D(priority_encoder_1_out), .Q(INT_addr), .clk(INT_in), .clr(register_1_q));  // open: en

  assign INT_out = INT_in;
endmodule

module ALU (
  input  [15:0] in1,
  input  [15:0] in2,
  input  [2:0] ALU_EXTRA,
  input  [2:0] ALUSEL,
  output [15:0] out,
  output ZF
);

  wire or_2_out;
  wire [15:0] adder_1_out, adder_2_out, and_1_out, multiplexer_2_out, not_1_out, or_1_out, subtractor_1_out,
       subtractor_2_out, xor_1_out;

  Adder #(.width(16)) adder_1 (.a(in1), .b(in2), .out(adder_1_out));  // open: cin, cout
  Subtractor #(.width(16)) subtractor_1 (.a(in1), .b(in2), .out(subtractor_1_out));  // open: bin, bout
  assign and_1_out = in1 & in2;  // AND_Gate and_1, 16 bits wide
  assign or_1_out = in1 | in2;  // OR_Gate or_1, 16 bits wide
  Multiplexer #(.select(3), .width(16), .enable("false")) multiplexer_1 (
    .in0(adder_1_out), .in1(subtractor_1_out), .in2(and_1_out), .in3(or_1_out), .in4(xor_1_out),
    .in7(multiplexer_2_out), .out(out), .sel(ALUSEL));  // open: in5, in6
  assign xor_1_out = in1 ^ in2;  // XOR_Gate xor_1, 16 bits wide
  assign not_1_out = ~in1;  // NOT_Gate not_1, 16 bits wide
  Multiplexer #(.select(3), .width(16), .enable("false")) multiplexer_2 (
    .in0(in1), .in1(not_1_out), .in2(adder_2_out), .in3(subtractor_2_out), .out(multiplexer_2_out),
    .sel(ALU_EXTRA));  // open: in4, in5, in6, in7
  Adder #(.width(16)) adder_2 (.a(in1), .b(16'h1), .out(adder_2_out));  // open: cin, cout
  or or_2 (or_2_out, out[0], out[1], out[2], out[3], out[4], out[5], out[6], out[7], out[8], out[9], out[10], out[11], out[12], out[13], out[14], out[15]);
  not not_2 (ZF, or_2_out);
  Subtractor #(.width(16)) subtractor_2 (.a(in1), .b(16'h1), .out(subtractor_2_out));  // open: bin, bout
endmodule

// PC
module pc (
  input  clk,
  input  [11:0] \input ,
  input  PC_LD,
  input  PC_INC,
  output [11:0] out
);

  wire or_1_out;
  wire [11:0] adder_1_out, multiplexer_1_out;

  Multiplexer #(.width(12), .enable("false")) multiplexer_1 (
    .in0(adder_1_out), .in1(\input ), .out(multiplexer_1_out), .sel(PC_LD));
  Adder #(.width(12)) adder_1 (.a(out), .b(12'h1), .out(adder_1_out));  // open: cin, cout
  _12_bit_register pc_Register (.clk(clk), .D(multiplexer_1_out), .load(or_1_out), .Q(out));
  or or_1 (or_1_out, PC_LD, PC_INC);
endmodule

module interrupt_register (
  input  sti,
  input  cli,
  input  clk,
  input  REGLD,
  input  ZF,
  input  [15:0] in,
  input  ZFLD,
  input  FLAGLD,
  output IF,
  output [15:0] out
);

  wire and_1_out, and_2_out, and_3_out, and_4_out, multiplexer_1_out, multiplexer_2_out, not_1_out,
       not_2_out, or_1_out, or_2_out, or_3_out, or_4_out;

  or or_1 (or_1_out, sti, cli, FLAGLD);
  or or_2 (or_2_out, REGLD, or_1_out);
  not not_1 (not_1_out, multiplexer_1_out);
  Multiplexer #(.enable("false")) multiplexer_1 (.in0(sti), .in1(in[1]), .out(multiplexer_1_out), .sel(or_3_out));
  or or_3 (or_3_out, REGLD, FLAGLD);
  and and_1 (and_1_out, multiplexer_1_out, or_2_out);
  and and_2 (and_2_out, not_1_out, or_2_out);
  S_R_Flip_Flop s_r_ff_1 (.S(and_1_out), .clk(clk), .R(and_2_out), .Q(IF));  // open: Qn, preset, reset, en
  Multiplexer #(.enable("false")) multiplexer_2 (.in0(in[0]), .in1(ZF), .out(multiplexer_2_out), .sel(ZFLD));
  and and_3 (and_3_out, multiplexer_2_out, or_4_out);
  not not_2 (not_2_out, multiplexer_2_out);
  and and_4 (and_4_out, not_2_out, or_4_out);
  or or_4 (or_4_out, ZFLD, FLAGLD);
  S_R_Flip_Flop s_r_ff_2 (.S(and_3_out), .clk(clk), .R(and_4_out), .Q(out[0]));  // open: Qn, preset, reset, en

  assign out[15:1] = {{14{1'b0}}, IF};

  // Notes on the sheet:
  //   D[1]
  //   D[0]
endmodule

// IR
module _16_bit_register (
  input  [15:0] D,
  input  load,
  input  clock,
  output [15:0] Q
);

  wire not_1_out, not_2_out, not_3_out, not_4_out, not_5_out, not_6_out, not_7_out, not_8_out, not_9_out,
       not_10_out, not_11_out, not_12_out, not_13_out, not_14_out, not_15_out, not_16_out;

  not not_1 (not_1_out, D[6]);
  not not_2 (not_2_out, D[5]);
  not not_3 (not_3_out, D[0]);
  not not_4 (not_4_out, D[2]);
  not not_5 (not_5_out, D[1]);
  not not_6 (not_6_out, D[4]);
  not not_7 (not_7_out, D[3]);
  not not_8 (not_8_out, D[7]);
  not not_9 (not_9_out, D[10]);
  not not_10 (not_10_out, D[13]);
  not not_11 (not_11_out, D[8]);
  not not_12 (not_12_out, D[12]);
  not not_13 (not_13_out, D[14]);
  not not_14 (not_14_out, D[9]);
  not not_15 (not_15_out, D[11]);
  not not_16 (not_16_out, D[15]);
  S_R_Flip_Flop s_r_ff_1 (.S(D[1]), .clk(clock), .R(not_5_out), .Q(Q[1]), .en(load));  // open: Qn, preset, reset
  S_R_Flip_Flop s_r_ff_2 (.S(D[3]), .clk(clock), .R(not_7_out), .Q(Q[3]), .en(load));  // open: Qn, preset, reset
  S_R_Flip_Flop s_r_ff_3 (.S(D[5]), .clk(clock), .R(not_2_out), .Q(Q[5]), .en(load));  // open: Qn, preset, reset
  S_R_Flip_Flop s_r_ff_4 (.S(D[7]), .clk(clock), .R(not_8_out), .Q(Q[7]), .en(load));  // open: Qn, preset, reset
  S_R_Flip_Flop s_r_ff_5 (.S(D[9]), .clk(clock), .R(not_14_out), .Q(Q[9]), .en(load));  // open: Qn, preset, reset
  S_R_Flip_Flop s_r_ff_6 (.S(D[11]), .clk(clock), .R(not_15_out), .Q(Q[11]), .en(load));  // open: Qn, preset, reset
  S_R_Flip_Flop s_r_ff_7 (.S(D[13]), .clk(clock), .R(not_10_out), .Q(Q[13]), .en(load));  // open: Qn, preset, reset
  S_R_Flip_Flop s_r_ff_8 (.S(D[15]), .clk(clock), .R(not_16_out), .Q(Q[15]), .en(load));  // open: Qn, preset, reset
  S_R_Flip_Flop s_r_ff_9 (.S(D[0]), .clk(clock), .R(not_3_out), .Q(Q[0]), .en(load));  // open: Qn, preset, reset
  S_R_Flip_Flop s_r_ff_10 (.S(D[2]), .clk(clock), .R(not_4_out), .Q(Q[2]), .en(load));  // open: Qn, preset, reset
  S_R_Flip_Flop s_r_ff_11 (.S(D[4]), .clk(clock), .R(not_6_out), .Q(Q[4]), .en(load));  // open: Qn, preset, reset
  S_R_Flip_Flop s_r_ff_12 (.S(D[6]), .clk(clock), .R(not_1_out), .Q(Q[6]), .en(load));  // open: Qn, preset, reset
  S_R_Flip_Flop s_r_ff_13 (.S(D[8]), .clk(clock), .R(not_11_out), .Q(Q[8]), .en(load));  // open: Qn, preset, reset
  S_R_Flip_Flop s_r_ff_14 (.S(D[10]), .clk(clock), .R(not_9_out), .Q(Q[10]), .en(load));  // open: Qn, preset, reset
  S_R_Flip_Flop s_r_ff_15 (.S(D[12]), .clk(clock), .R(not_12_out), .Q(Q[12]), .en(load));  // open: Qn, preset, reset
  S_R_Flip_Flop s_r_ff_16 (.S(D[14]), .clk(clock), .R(not_13_out), .Q(Q[14]), .en(load));  // open: Qn, preset, reset

  // Other names for the same wires on the sheet: a[8:0] = D[8:0]; b[6:0] = D[15:9]
endmodule

module _12_bit_register (
  input  clk,
  input  [11:0] D,
  input  load,
  output [11:0] Q
);

  wire not_1_out, not_2_out, not_3_out, not_4_out, not_5_out, not_6_out, not_7_out, not_8_out, not_9_out,
       not_10_out, not_11_out, not_12_out;

  not not_1 (not_1_out, D[0]);
  not not_2 (not_2_out, D[1]);
  not not_3 (not_3_out, D[2]);
  not not_4 (not_4_out, D[3]);
  not not_5 (not_5_out, D[4]);
  not not_6 (not_6_out, D[5]);
  not not_7 (not_7_out, D[6]);
  not not_8 (not_8_out, D[7]);
  not not_9 (not_9_out, D[8]);
  not not_10 (not_10_out, D[9]);
  not not_11 (not_11_out, D[10]);
  not not_12 (not_12_out, D[11]);
  S_R_Flip_Flop s_r_ff_1 (.S(D[0]), .clk(clk), .R(not_1_out), .Q(Q[0]), .en(load));  // open: Qn, preset, reset
  S_R_Flip_Flop s_r_ff_2 (.S(D[1]), .clk(clk), .R(not_2_out), .Q(Q[1]), .en(load));  // open: Qn, preset, reset
  S_R_Flip_Flop s_r_ff_3 (.S(D[2]), .clk(clk), .R(not_3_out), .Q(Q[2]), .en(load));  // open: Qn, preset, reset
  S_R_Flip_Flop s_r_ff_4 (.S(D[3]), .clk(clk), .R(not_4_out), .Q(Q[3]), .en(load));  // open: Qn, preset, reset
  S_R_Flip_Flop s_r_ff_5 (.S(D[4]), .clk(clk), .R(not_5_out), .Q(Q[4]), .en(load));  // open: Qn, preset, reset
  S_R_Flip_Flop s_r_ff_6 (.S(D[5]), .clk(clk), .R(not_6_out), .Q(Q[5]), .en(load));  // open: Qn, preset, reset
  S_R_Flip_Flop s_r_ff_7 (.S(D[6]), .clk(clk), .R(not_7_out), .Q(Q[6]), .en(load));  // open: Qn, preset, reset
  S_R_Flip_Flop s_r_ff_8 (.S(D[7]), .clk(clk), .R(not_8_out), .Q(Q[7]), .en(load));  // open: Qn, preset, reset
  S_R_Flip_Flop s_r_ff_9 (.S(D[8]), .clk(clk), .R(not_9_out), .Q(Q[8]), .en(load));  // open: Qn, preset, reset
  S_R_Flip_Flop s_r_ff_10 (.S(D[9]), .clk(clk), .R(not_10_out), .Q(Q[9]), .en(load));  // open: Qn, preset, reset
  S_R_Flip_Flop s_r_ff_11 (.S(D[10]), .clk(clk), .R(not_11_out), .Q(Q[10]), .en(load));  // open: Qn, preset, reset
  S_R_Flip_Flop s_r_ff_12 (.S(D[11]), .clk(clk), .R(not_12_out), .Q(Q[11]), .en(load));  // open: Qn, preset, reset
endmodule

// POP CLEAR
module POP (
  input  clk,
  input  [15:0] Din,
  output Dout
);

  wire iret1_2_out, iret1_out, not_1_out, not_2_out, not_3_out, not_4_out, not_5_out, not_6_out, not_7_out,
       or_1_out, pop_out, register_1_q, register_2_q, register_3_q, register_4_q, register_5_q, register_6_q,
       register_7_q, register_8_q, register_9_q, register_10_q, register_11_q, register_12_q, ret_out;

  not not_1 (not_1_out, Din[13]);
  not not_2 (not_2_out, Din[14]);
  not not_3 (not_3_out, Din[14]);
  not not_4 (not_4_out, Din[12]);
  not not_5 (not_5_out, Din[15]);
  and pop (pop_out, Din[12], not_1_out, not_2_out, Din[15]);
  and ret (ret_out, Din[12], Din[13], not_3_out, Din[15]);
  and iret1 (iret1_out, not_4_out, Din[13], Din[14], not_5_out);
  or or_1 (or_1_out, pop_out, ret_out);
  Register #(.width(1)) register_1 (.D(or_1_out), .Q(register_1_q), .clk(clk));  // open: en, clr
  Register #(.width(1)) register_2 (.D(register_1_q), .Q(register_2_q), .clk(clk), .clr(register_3_q));  // open: en
  Register #(.width(1)) register_3 (.D(register_2_q), .Q(register_3_q), .clk(clk));  // open: en, clr
  Register #(.width(1)) register_4 (.D(iret1_out), .Q(register_4_q), .clk(clk));  // open: en, clr
  Register #(.width(1)) register_5 (.D(register_4_q), .Q(register_5_q), .clk(clk));  // open: en, clr
  Register #(.width(1)) register_6 (.D(register_5_q), .Q(register_6_q), .clk(clk), .clr(register_7_q));  // open: en
  Register #(.width(1)) register_7 (.D(register_6_q), .Q(register_7_q), .clk(clk));  // open: en, clr
  not not_6 (not_6_out, Din[12]);
  and iret1_2 (iret1_2_out, not_6_out, Din[13], Din[14], not_7_out);
  not not_7 (not_7_out, Din[15]);
  Register #(.width(1)) register_8 (.D(iret1_2_out), .Q(register_8_q), .clk(clk));  // open: en, clr
  Register #(.width(1)) register_9 (.D(register_8_q), .Q(register_9_q), .clk(clk));  // open: en, clr
  or or_2 (Dout, register_2_q, register_6_q, register_11_q);
  Register #(.width(1)) register_10 (.D(register_9_q), .Q(register_10_q), .clk(clk));  // open: en, clr
  Register #(.width(1)) register_11 (.D(register_10_q), .Q(register_11_q), .clk(clk), .clr(register_12_q));  // open: en
  Register #(.width(1)) register_12 (.D(register_11_q), .Q(register_12_q), .clk(clk));  // open: en, clr

  // Notes on the sheet:
  //   If the OPCODE=POP or OPCODE=RET or OPCODE=IRET, then after 2 clock cycles the content of the current address will be zero.
endmodule

// addr
module addr_mux (
  input  [4:0] in,
  output [1:0] out
);

  wire _2_out, _3_out, _8_out, _10_out, _12_out, _13_out, _16_out, _18_out, _19_out, _20_out, _21_out,
       not_1_out, not_2_out, not_3_out, not_4_out, not_5_out, not_6_out, not_7_out, not_8_out, not_9_out,
       not_10_out, not_11_out, not_12_out, not_13_out, not_14_out, not_15_out, not_16_out, not_17_out,
       not_18_out, not_19_out, not_20_out, not_21_out, not_22_out, not_23_out, not_24_out, not_25_out,
       not_26_out, not_27_out, not_28_out, not_29_out, not_30_out, not_31_out, not_32_out, not_33_out,
       or_1_out, priority_encoder_1_p2;

  not not_1 (not_1_out, in[3]);
  not not_2 (not_2_out, in[0]);
  not not_3 (not_3_out, in[3]);
  not not_4 (not_4_out, in[1]);
  not not_5 (not_5_out, in[1]);
  and _20 (_20_out, in[4], not_1_out, in[2], not_4_out, not_2_out);
  and _21 (_21_out, in[4], not_3_out, in[2], not_5_out, in[0]);
  not not_6 (not_6_out, in[3]);
  not not_7 (not_7_out, in[2]);
  and _19 (_19_out, in[4], not_6_out, not_7_out, in[1], in[0]);
  not not_8 (not_8_out, in[3]);
  not not_9 (not_9_out, in[3]);
  not not_10 (not_10_out, in[2]);
  not not_11 (not_11_out, in[0]);
  and _18 (_18_out, in[4], not_8_out, not_10_out, in[1], not_11_out);
  not not_12 (not_12_out, in[2]);
  not not_13 (not_13_out, in[4]);
  not not_14 (not_14_out, in[0]);
  not not_15 (not_15_out, in[1]);
  not not_16 (not_16_out, in[1]);
  and _13 (_13_out, not_13_out, in[3], in[2], not_16_out, in[0]);
  and _16 (_16_out, in[4], not_9_out, not_12_out, not_15_out, not_14_out);
  or or_1 (or_1_out, _21_out, _19_out, _18_out, _16_out, _13_out, _12_out, _10_out, _8_out);
  // Priority_Encoder #(.select(2)) priority_encoder_1: pin names not known; wires that end beside it: 1'b1, priority_encoder_1_p2, out, or_1_out, _20_out
  not not_17 (not_17_out, in[1]);
  not not_18 (not_18_out, in[0]);
  not not_19 (not_19_out, in[4]);
  and _12 (_12_out, not_19_out, in[3], in[2], not_17_out, not_18_out);
  not not_20 (not_20_out, in[4]);
  not not_21 (not_21_out, in[4]);
  not not_22 (not_22_out, in[2]);
  not not_23 (not_23_out, in[0]);
  and _10 (_10_out, not_20_out, in[3], not_22_out, in[1], not_23_out);
  not not_24 (not_24_out, in[2]);
  not not_25 (not_25_out, in[1]);
  not not_26 (not_26_out, in[3]);
  not not_27 (not_27_out, in[2]);
  not not_28 (not_28_out, in[0]);
  not not_29 (not_29_out, in[4]);
  and _8 (_8_out, not_21_out, in[3], not_24_out, not_25_out, not_28_out);
  and _3 (_3_out, not_29_out, not_26_out, not_27_out, in[1], in[0]);
  not not_30 (not_30_out, in[0]);
  not not_31 (not_31_out, in[4]);
  not not_32 (not_32_out, in[3]);
  not not_33 (not_33_out, in[2]);
  and _2 (_2_out, not_30_out, in[1], not_33_out, not_32_out, not_31_out);
  or or_2 (priority_encoder_1_p2, _3_out, _2_out);
endmodule

// data
module data_mux (
  input  [4:0] in,
  output [1:0] out
);

  wire _3_out, _8_out, _16_out, _18_out, not_1_out, not_2_out, not_3_out, not_4_out, not_5_out, not_6_out,
       not_7_out, not_8_out, not_9_out, not_10_out, not_11_out, not_12_out, not_13_out, not_14_out, or_1_out;

  not not_1 (not_1_out, in[1]);
  not not_2 (not_2_out, in[2]);
  not not_3 (not_3_out, in[3]);
  not not_4 (not_4_out, in[0]);
  and _16 (_16_out, in[4], not_3_out, not_2_out, not_1_out, not_4_out);
  not not_5 (not_5_out, in[3]);
  not not_6 (not_6_out, in[4]);
  not not_7 (not_7_out, in[0]);
  not not_8 (not_8_out, in[2]);
  and _18 (_18_out, in[4], not_5_out, not_8_out, in[1], not_7_out);
  not not_9 (not_9_out, in[4]);
  not not_10 (not_10_out, in[1]);
  not not_11 (not_11_out, in[2]);
  not not_12 (not_12_out, in[2]);
  not not_13 (not_13_out, in[3]);
  not not_14 (not_14_out, in[0]);
  and _8 (_8_out, not_6_out, in[3], not_11_out, not_10_out, not_14_out);
  and _3 (_3_out, not_9_out, not_13_out, not_12_out, in[1], in[0]);
  or or_1 (or_1_out, _8_out, _3_out);
  // Priority_Encoder #(.select(2)) priority_encoder_1: pin names not known; wires that end beside it: _16_out, 1'b1, or_1_out, out, _18_out
endmodule
